# Fritzing sketch ws (saved by Fritzing 0.9.3b)
breadboards: 1

parts:
  U2 = ESP8266 WiFi Module [part_number=ESP8266]
  DHT-22 = Humidity and Temperature Sensor RHT03
  R3 = Photocell (LDR) [package=THT]
  R4 = Resistor [tolerance=±5% resistance=220 package=THT]
  C2 = Tantalum Capacitor [capacitance=10nF voltage=16V package="100 mil [THT, tantalum]"]
  R5 = Resistor [tolerance=±5% resistance=10k package=THT]
  C1 = Electrolytic Capacitor [capacitance=100µF voltage=16V package="100 mil [THT, electrolytic]"]
  R7 = Resistor [tolerance=±5% resistance=10k package=THT]
  R8 = Resistor [tolerance=±5% resistance=10k package=THT]
  R9 = Resistor [tolerance=±5% resistance=10k package=THT]
  R10 = Resistor [tolerance=±5% resistance=10k package=THT]
  R11 = Resistor [tolerance=±5% resistance=10k package=THT]
  R12 = Resistor [tolerance=±5% resistance=220 package=THT]
  R14 = Resistor [tolerance=±5% resistance=10k package=THT]
  V1 = DC Power [voltage=3.3V]
  R15 = Resistor [tolerance=±5% resistance=100 package=THT]
  LED = LED - 3mm [color="Green (565nm)" package="3 mm [THT]"]

nets:
  VCC: U2.VCC, DHT-22.Vcc, C2.+, R5.Pin_0, C1.+, R7.Pin_0, R8.Pin_0, R9.Pin_0, R11.Pin_0, R12.Pin_0, V1.V+
  N1: U2.GPIO_0, R7.Pin_1
  N2: U2.GPIO_2, R8.Pin_1
  N3: U2.CH_PD, R9.Pin_1
  N4: U2.GND, DHT-22.GND_2, R4.Pin_1, C2.-, C1.-, R10.Pin_1, R14.Pin_1, V1.V-, R15.Pin_1
  N5: U2.GPIO_15, R10.Pin_0
  N6: U2.GPIO_4, LED.anode
  N7: U2.GPIO_5, DHT-22.Data-signal, R11.Pin_1
  N8: U2.ADC_0, R3.pin_0, R14.Pin_0
  N9: U2.REST, R5.Pin_1
  N10: R3.pin_1, R12.Pin_1, R15.Pin_0
  N11: R4.Pin_0, LED.cathode
